# Fritzing sketch Untitled Sketch (saved by Fritzing 0.9.3b)

parts:
  ENV1 = ENV Sensor
  M5stack1 = M5GO
  Earth1 = Earth

nets:
  N1: ENV1.GND, M5stack1.pin1
  N2: ENV1.VCC, M5stack1.pin2
  N3: ENV1.SDA, M5stack1.pin3
  N4: ENV1.SCL, M5stack1.pin4
  N5: M5stack1.pin5, Earth1.GND
  N6: M5stack1.pin6, Earth1.VCC
  N7: M5stack1.pin7, Earth1.IN#2
  N8: M5stack1.pin8, Earth1.IN#3

custom parts:
  ENV Sensor: An environmental sensor which is capable of sensing temperature, humidity and air pressure. Based on the DH12 sensor.
  M5GO: M5GO is a modular stackable development kit
  Earth: The Earth sensor is a volumetric moisture sensor predominately used for testing the moisture levels in soil.
